# Fritzing sketch IOTSEIS785 (saved by Fritzing 0.9.2b)
breadboards: 1

parts:
  Part1 = Photon
  PART1 = Sound Detector
  LED1 = RGB LED - (4 legs) [package="5 mm [THT]"]
  R1 = Resistor [tolerance=±5% resistance=330 package="2512 [SMD]"]
  R2 = Resistor [tolerance=±5% resistance=330 package="2010 [SMD]"]
  R3 = Resistor [tolerance=±5% resistance=330 package="2010 [SMD]"]
  LED2 = smd LED [color="Red (633nm)" package="0603 [SMD]"]
  R4 = Resistor [tolerance=±5% resistance=330 package="2010 [SMD]"]

nets:
  N1: Part1.A0, PART1.ENVELOPE
  N2: Part1.RX, PART1.AUDIO
  GND: Part1.GND, PART1.GND, LED1.red_cathode, LED2.cathode
  N3: Part1.D0, LED1.common_anode, R3.Pin_0, R3.Pin_1
  N4: Part1.D1, LED1.green_cathode, R2.Pin_0, R2.Pin_1
  N5: Part1.D2, LED1.blue_cathode, R1.Pin_0, R1.Pin_1
  N6: Part1.D3, PART1.GATE
  N7: Part1.D7, LED2.anode, R4.Pin_0, R4.Pin_1
  3V3: Part1.3V3, PART1.VCC

custom parts:
  Sound Detector: Electret microphone with multiple outputs. - First output is the actual audio - Second output is the amplitude envelope - Third output is a binary "sound present" indication - high while sound is present, low otherwise. Visit sparkfun.com for more documentations.

// code stored in the sketch: sounddetector.ino
// This #include statement was automatically added by the Particle IDE.
#include "rgb-controls/rgb-controls.h"
using namespace RGBControls;

// This #include statement was automatically added by the Particle IDE.
#include "MQTT/MQTT.h"

// Define hardware connections
int PIN_GATE_IN = D3;
int PIN_LED_OUT = D7;
int IRQ_GATE_IN = RX;
int PIN_ANALOG_IN = A0;

Led led(D0, D1, D2);
Color red(255, 0, 0);
Color green(0, 255, 0);
Color yellow(255, 255, 0);
Color white(255, 255, 255);
Color none(0, 0, 0);
Color currentColor(0, 0, 0);

void callback(char* topic, byte* payload, unsigned int length);
MQTT client("52.34.171.0", 1883, callback);

void debug(String message, int value) {
    char msg [100];
    sprintf(msg,message.c_str(), value);
    Spark.publish("DEBUG", msg);
}
 




//Show Color
void showColor(){
    led.setColor(currentColor);
    delay(1000);
}



//Receive messages from MQ
void callback(char* topic, byte* payload, unsigned int length) {
    char p[length + 1];
    memcpy(p, payload, length);
    p[length] = NULL;
    String message(p);
    debug(message, 1);    
    
    if(message.equals("red")){
        currentColor = red;
    } else if(message.equals("yellow")){
       currentColor = yellow;
    } else if(message.equals("green")){
        currentColor = green;
    } else {
        currentColor = white;
    }
    showColor();
    delay(1000);
}


// soundISR()
// This function is installed as an interrupt service routine for the pin
// change interrupt.  When digital input 2 changes state, this routine
// is called.
// It queries the state of that pin, and sets the onboard LED to reflect that 
// pin's state.
void soundISR()
{
  int pin_val;
  pin_val = digitalRead(PIN_GATE_IN);
  digitalWrite(PIN_LED_OUT, pin_val);
}



void setup()
{
  // configure input to interrupt
  pinMode(PIN_GATE_IN, INPUT);
  pinMode(PIN_LED_OUT, OUTPUT);
  attachInterrupt(PIN_GATE_IN, soundISR, CHANGE);
  currentColor = white;
  showColor();
  client.connect("music_teacher");
  if(client.isConnected()){
     client.subscribe("practice_status");
  }
}

void loop()
{

  //MQTT
  if(client.isConnected()){
        client.loop();
  }

  
  int value = 0;
  long duration = 0;
  
  // Check the envelope input
  duration = pulseIn(PIN_GATE_IN, HIGH);
  value = analogRead(PIN_ANALOG_IN);
     
  // Convert envelope value into a message
  if(duration > 0){
    char message [255];
   snprintf(message, sizeof(message),"{\"type\":\"mic_sensor\",\"message\":\"duration_log\",\"product\":\"music_teacher\",\"value\":\"%d\"}",duration);
   if(client.isConnected()){
       debug("duration=>%d", duration); 
       client.publish("events_messages",message);
       delay(1000);
   }
  }
  // pause for 1 second
  delay(1000);
}
